// Digital circuit 1-Bit ALU.dig as structural Verilog
module _1_Bit_ALU (
  input  A,
  input  B,
  input  A_Invert,
  input  B_Invert,
  input  Cin,
  input  Less,
  input  [1:0] Operation,
  output Set,
  output Cout,
  output Result
);

  wire and_1_out, multiplexer_1_out, multiplexer_2_out, not_1_out, not_2_out, or_1_out;

  not not_1 (not_1_out, A);
  not not_2 (not_2_out, B);
  Multiplexer multiplexer_1 (.sel(A_Invert), .in_0(A), .in_1(not_1_out), .out(multiplexer_1_out));
  Multiplexer multiplexer_2 (.sel(B_Invert), .in_0(B), .in_1(not_2_out), .out(multiplexer_2_out));
  and and_1 (and_1_out, multiplexer_1_out, multiplexer_2_out);
  or or_1 (or_1_out, multiplexer_1_out, multiplexer_2_out);
  _1_Bit_Full_Adder _1_bit_full_adder_1 (.A(multiplexer_1_out), .B(multiplexer_2_out), .Cin(Cin), .S(Set), .Cout(Cout));
  Multiplexer #(.Selector_Bits(2)) multiplexer_3 (
    .sel(Operation), .in_0(and_1_out), .in_1(or_1_out), .in_2(Set), .in_3(Less), .out(Result));
endmodule
