// Digital circuit 1-Bit-Register.dig as structural Verilog
module _1_Bit_Register (
  input  D,
  input  CLK,
  output Q,
  output Q_2
);

  wire d_ff_1_q, not_1_out;

  not not_1 (not_1_out, CLK);
  D_FF d_ff_1 (.D(D), .C(not_1_out), .Q(d_ff_1_q));  // open: nQ
  D_FF d_ff_2 (.D(d_ff_1_q), .C(CLK), .Q(Q), .nQ(Q_2));
endmodule
