// Digital circuit 256x32bit Memory.dig as structural Verilog
module _256x32bit_Memory (
  input  [31:0] Address,
  input  Write_Enable,
  input  [31:0] Write_Data,
  input  Clock,
  output [31:0] Read_Data
);

  wire and_1_out, and_2_out, and_3_out, and_4_out, and_5_out, and_6_out, and_7_out, and_8_out,
       decoder_1_out_0, decoder_1_out_1, decoder_1_out_2, decoder_1_out_3, decoder_1_out_4, decoder_1_out_5,
       decoder_1_out_6, decoder_1_out_7;
  wire [31:0] _32_32_bit_register_file_1_read_data_1, _32_32_bit_register_file_2_read_data_1,
       _32_32_bit_register_file_3_read_data_1, _32_32_bit_register_file_4_read_data_1,
       _32_32_bit_register_file_5_read_data_1, _32_32_bit_register_file_6_read_data_1,
       _32_32_bit_register_file_7_read_data_1, _32_32_bit_register_file_8_read_data_1;

  Decoder #(.Selector_Bits(3)) decoder_1 (
    .sel(Address[7:5]), .out_0(decoder_1_out_0), .out_1(decoder_1_out_1), .out_2(decoder_1_out_2),
    .out_3(decoder_1_out_3), .out_4(decoder_1_out_4), .out_5(decoder_1_out_5), .out_6(decoder_1_out_6),
    .out_7(decoder_1_out_7));
  and and_1 (and_1_out, Write_Enable, decoder_1_out_0);
  and and_2 (and_2_out, Write_Enable, decoder_1_out_1);
  and and_3 (and_3_out, Write_Enable, decoder_1_out_2);
  and and_4 (and_4_out, Write_Enable, decoder_1_out_3);
  and and_5 (and_5_out, Write_Enable, decoder_1_out_4);
  and and_6 (and_6_out, Write_Enable, decoder_1_out_5);
  and and_7 (and_7_out, Write_Enable, decoder_1_out_6);
  and and_8 (and_8_out, Write_Enable, decoder_1_out_7);
  _32_32_bit_Register_File _32_32_bit_register_file_1 (
    .Read_Register_Number_1(Address[4:0]), .Read_Register_Number_2({5{1'b0}}), .Write_Data(Write_Data),
    .Write_Enable(and_1_out), .Write_Register_Number(Address[4:0]), .Clock(Clock),
    .Read_Data_1(_32_32_bit_register_file_1_read_data_1));  // open: Read_Data_2
  _32_32_bit_Register_File _32_32_bit_register_file_2 (
    .Read_Register_Number_1(Address[4:0]), .Read_Register_Number_2({5{1'b0}}), .Write_Data(Write_Data),
    .Write_Enable(and_2_out), .Write_Register_Number(Address[4:0]), .Clock(Clock),
    .Read_Data_1(_32_32_bit_register_file_2_read_data_1));  // open: Read_Data_2
  _32_32_bit_Register_File _32_32_bit_register_file_3 (
    .Read_Register_Number_1(Address[4:0]), .Read_Register_Number_2({5{1'b0}}), .Write_Data(Write_Data),
    .Write_Enable(and_3_out), .Write_Register_Number(Address[4:0]), .Clock(Clock),
    .Read_Data_1(_32_32_bit_register_file_3_read_data_1));  // open: Read_Data_2
  _32_32_bit_Register_File _32_32_bit_register_file_4 (
    .Read_Register_Number_1(Address[4:0]), .Read_Register_Number_2({5{1'b0}}), .Write_Data(Write_Data),
    .Write_Enable(and_4_out), .Write_Register_Number(Address[4:0]), .Clock(Clock),
    .Read_Data_1(_32_32_bit_register_file_4_read_data_1));  // open: Read_Data_2
  _32_32_bit_Register_File _32_32_bit_register_file_5 (
    .Read_Register_Number_1(Address[4:0]), .Read_Register_Number_2({5{1'b0}}), .Write_Data(Write_Data),
    .Write_Enable(and_5_out), .Write_Register_Number(Address[4:0]), .Clock(Clock),
    .Read_Data_1(_32_32_bit_register_file_5_read_data_1));  // open: Read_Data_2
  _32_32_bit_Register_File _32_32_bit_register_file_6 (
    .Read_Register_Number_1(Address[4:0]), .Read_Register_Number_2({5{1'b0}}), .Write_Data(Write_Data),
    .Write_Enable(and_6_out), .Write_Register_Number(Address[4:0]), .Clock(Clock),
    .Read_Data_1(_32_32_bit_register_file_6_read_data_1));  // open: Read_Data_2
  _32_32_bit_Register_File _32_32_bit_register_file_7 (
    .Read_Register_Number_1(Address[4:0]), .Read_Register_Number_2({5{1'b0}}), .Write_Data(Write_Data),
    .Write_Enable(and_7_out), .Write_Register_Number(Address[4:0]), .Clock(Clock),
    .Read_Data_1(_32_32_bit_register_file_7_read_data_1));  // open: Read_Data_2
  _32_32_bit_Register_File _32_32_bit_register_file_8 (
    .Read_Register_Number_1(Address[4:0]), .Read_Register_Number_2({5{1'b0}}), .Write_Data(Write_Data),
    .Write_Enable(and_8_out), .Write_Register_Number(Address[4:0]), .Clock(Clock),
    .Read_Data_1(_32_32_bit_register_file_8_read_data_1));  // open: Read_Data_2
  assign Read_Data = decoder_1_out_0 ? _32_32_bit_register_file_1_read_data_1 : 32'bz;  // Driver driver_1
  assign Read_Data = decoder_1_out_1 ? _32_32_bit_register_file_2_read_data_1 : 32'bz;  // Driver driver_2
  assign Read_Data = decoder_1_out_2 ? _32_32_bit_register_file_3_read_data_1 : 32'bz;  // Driver driver_3
  assign Read_Data = decoder_1_out_3 ? _32_32_bit_register_file_4_read_data_1 : 32'bz;  // Driver driver_4
  assign Read_Data = decoder_1_out_4 ? _32_32_bit_register_file_5_read_data_1 : 32'bz;  // Driver driver_5
  assign Read_Data = decoder_1_out_5 ? _32_32_bit_register_file_6_read_data_1 : 32'bz;  // Driver driver_6
  assign Read_Data = decoder_1_out_6 ? _32_32_bit_register_file_7_read_data_1 : 32'bz;  // Driver driver_7
  assign Read_Data = decoder_1_out_7 ? _32_32_bit_register_file_8_read_data_1 : 32'bz;  // Driver driver_8
endmodule
