// Digital circuit 32 32-bit Register File.dig as structural Verilog
module _32_32_bit_Register_File (
  input  [4:0] Read_Register_Number_1,
  input  [4:0] Read_Register_Number_2,
  input  [31:0] Write_Data,
  input  Write_Enable,
  input  [4:0] Write_Register_Number,
  input  Clock,
  output [31:0] Read_Data_1,
  output [31:0] Read_Data_2
);

  wire and_1_out, and_2_out, and_3_out, and_4_out, and_5_out, and_6_out, and_7_out, and_8_out, and_9_out,
       and_10_out, and_11_out, and_12_out, and_13_out, and_14_out, and_15_out, and_16_out, and_17_out,
       and_18_out, and_19_out, and_20_out, and_21_out, and_22_out, and_23_out, and_24_out, and_25_out,
       and_26_out, and_27_out, and_28_out, and_29_out, and_30_out, and_31_out, and_32_out, decoder_1_out_0,
       decoder_1_out_1, decoder_1_out_2, decoder_1_out_3, decoder_1_out_4, decoder_1_out_5, decoder_1_out_6,
       decoder_1_out_7, decoder_1_out_8, decoder_1_out_9, decoder_1_out_10, decoder_1_out_11,
       decoder_1_out_12, decoder_1_out_13, decoder_1_out_14, decoder_1_out_15, decoder_1_out_16,
       decoder_1_out_17, decoder_1_out_18, decoder_1_out_19, decoder_1_out_20, decoder_1_out_21,
       decoder_1_out_22, decoder_1_out_23, decoder_1_out_24, decoder_1_out_25, decoder_1_out_26,
       decoder_1_out_27, decoder_1_out_28, decoder_1_out_29, decoder_1_out_30, decoder_1_out_31;
  wire [31:0] register_1_q, register_2_q, register_3_q, register_4_q, register_5_q, register_6_q,
       register_7_q, register_8_q, register_9_q, register_10_q, register_11_q, register_12_q, register_13_q,
       register_14_q, register_15_q, register_16_q, register_17_q, register_18_q, register_19_q,
       register_20_q, register_21_q, register_22_q, register_23_q, register_24_q, register_25_q,
       register_26_q, register_27_q, register_28_q, register_29_q, register_30_q, register_31_q,
       register_32_q;

  Decoder #(.Selector_Bits(5)) decoder_1 (
    .sel(Write_Register_Number), .out_0(decoder_1_out_0), .out_1(decoder_1_out_1), .out_2(decoder_1_out_2),
    .out_3(decoder_1_out_3), .out_4(decoder_1_out_4), .out_5(decoder_1_out_5), .out_6(decoder_1_out_6),
    .out_7(decoder_1_out_7), .out_8(decoder_1_out_8), .out_9(decoder_1_out_9), .out_10(decoder_1_out_10),
    .out_11(decoder_1_out_11), .out_12(decoder_1_out_12), .out_13(decoder_1_out_13),
    .out_14(decoder_1_out_14), .out_15(decoder_1_out_15), .out_16(decoder_1_out_16),
    .out_17(decoder_1_out_17), .out_18(decoder_1_out_18), .out_19(decoder_1_out_19),
    .out_20(decoder_1_out_20), .out_21(decoder_1_out_21), .out_22(decoder_1_out_22),
    .out_23(decoder_1_out_23), .out_24(decoder_1_out_24), .out_25(decoder_1_out_25),
    .out_26(decoder_1_out_26), .out_27(decoder_1_out_27), .out_28(decoder_1_out_28),
    .out_29(decoder_1_out_29), .out_30(decoder_1_out_30), .out_31(decoder_1_out_31));
  and and_1 (and_1_out, Write_Enable, decoder_1_out_0);
  and and_2 (and_2_out, Write_Enable, decoder_1_out_1);
  and and_3 (and_3_out, Write_Enable, decoder_1_out_2);
  and and_4 (and_4_out, Write_Enable, decoder_1_out_3);
  and and_5 (and_5_out, Write_Enable, decoder_1_out_4);
  and and_6 (and_6_out, Write_Enable, decoder_1_out_5);
  and and_7 (and_7_out, Write_Enable, decoder_1_out_6);
  and and_8 (and_8_out, Write_Enable, decoder_1_out_7);
  and and_9 (and_9_out, Write_Enable, decoder_1_out_8);
  and and_10 (and_10_out, Write_Enable, decoder_1_out_9);
  and and_11 (and_11_out, Write_Enable, decoder_1_out_10);
  and and_12 (and_12_out, Write_Enable, decoder_1_out_11);
  and and_13 (and_13_out, Write_Enable, decoder_1_out_12);
  and and_14 (and_14_out, Write_Enable, decoder_1_out_13);
  and and_15 (and_15_out, Write_Enable, decoder_1_out_14);
  and and_16 (and_16_out, Write_Enable, decoder_1_out_15);
  and and_17 (and_17_out, Write_Enable, decoder_1_out_16);
  and and_18 (and_18_out, Write_Enable, decoder_1_out_17);
  and and_19 (and_19_out, Write_Enable, decoder_1_out_18);
  and and_20 (and_20_out, Write_Enable, decoder_1_out_19);
  and and_21 (and_21_out, Write_Enable, decoder_1_out_20);
  and and_22 (and_22_out, Write_Enable, decoder_1_out_21);
  and and_23 (and_23_out, Write_Enable, decoder_1_out_22);
  and and_24 (and_24_out, Write_Enable, decoder_1_out_23);
  and and_25 (and_25_out, Write_Enable, decoder_1_out_24);
  and and_26 (and_26_out, Write_Enable, decoder_1_out_25);
  and and_27 (and_27_out, Write_Enable, decoder_1_out_26);
  and and_28 (and_28_out, Write_Enable, decoder_1_out_27);
  and and_29 (and_29_out, Write_Enable, decoder_1_out_28);
  and and_30 (and_30_out, Write_Enable, decoder_1_out_29);
  and and_31 (and_31_out, Write_Enable, decoder_1_out_30);
  and and_32 (and_32_out, Write_Enable, decoder_1_out_31);
  Register #(.Bits(32)) register_1 (.D(Write_Data), .C(Clock), .en(and_1_out), .Q(register_1_q));
  Register #(.Bits(32)) register_2 (.D(Write_Data), .C(Clock), .en(and_2_out), .Q(register_2_q));
  Register #(.Bits(32)) register_3 (.D(Write_Data), .C(Clock), .en(and_3_out), .Q(register_3_q));
  Register #(.Bits(32)) register_4 (.D(Write_Data), .C(Clock), .en(and_4_out), .Q(register_4_q));
  Register #(.Bits(32)) register_5 (.D(Write_Data), .C(Clock), .en(and_5_out), .Q(register_5_q));
  Register #(.Bits(32)) register_6 (.D(Write_Data), .C(Clock), .en(and_6_out), .Q(register_6_q));
  Register #(.Bits(32)) register_7 (.D(Write_Data), .C(Clock), .en(and_7_out), .Q(register_7_q));
  Register #(.Bits(32)) register_8 (.D(Write_Data), .C(Clock), .en(and_8_out), .Q(register_8_q));
  Register #(.Bits(32)) register_9 (.D(Write_Data), .C(Clock), .en(and_9_out), .Q(register_9_q));
  Register #(.Bits(32)) register_10 (.D(Write_Data), .C(Clock), .en(and_10_out), .Q(register_10_q));
  Register #(.Bits(32)) register_11 (.D(Write_Data), .C(Clock), .en(and_11_out), .Q(register_11_q));
  Register #(.Bits(32)) register_12 (.D(Write_Data), .C(Clock), .en(and_12_out), .Q(register_12_q));
  Register #(.Bits(32)) register_13 (.D(Write_Data), .C(Clock), .en(and_13_out), .Q(register_13_q));
  Register #(.Bits(32)) register_14 (.D(Write_Data), .C(Clock), .en(and_14_out), .Q(register_14_q));
  Register #(.Bits(32)) register_15 (.D(Write_Data), .C(Clock), .en(and_15_out), .Q(register_15_q));
  Register #(.Bits(32)) register_16 (.D(Write_Data), .C(Clock), .en(and_16_out), .Q(register_16_q));
  Register #(.Bits(32)) register_17 (.D(Write_Data), .C(Clock), .en(and_17_out), .Q(register_17_q));
  Register #(.Bits(32)) register_18 (.D(Write_Data), .C(Clock), .en(and_18_out), .Q(register_18_q));
  Register #(.Bits(32)) register_19 (.D(Write_Data), .C(Clock), .en(and_19_out), .Q(register_19_q));
  Register #(.Bits(32)) register_20 (.D(Write_Data), .C(Clock), .en(and_20_out), .Q(register_20_q));
  Register #(.Bits(32)) register_21 (.D(Write_Data), .C(Clock), .en(and_21_out), .Q(register_21_q));
  Register #(.Bits(32)) register_22 (.D(Write_Data), .C(Clock), .en(and_22_out), .Q(register_22_q));
  Register #(.Bits(32)) register_23 (.D(Write_Data), .C(Clock), .en(and_23_out), .Q(register_23_q));
  Register #(.Bits(32)) register_24 (.D(Write_Data), .C(Clock), .en(and_24_out), .Q(register_24_q));
  Register #(.Bits(32)) register_25 (.D(Write_Data), .C(Clock), .en(and_25_out), .Q(register_25_q));
  Register #(.Bits(32)) register_26 (.D(Write_Data), .C(Clock), .en(and_26_out), .Q(register_26_q));
  Register #(.Bits(32)) register_27 (.D(Write_Data), .C(Clock), .en(and_27_out), .Q(register_27_q));
  Register #(.Bits(32)) register_28 (.D(Write_Data), .C(Clock), .en(and_28_out), .Q(register_28_q));
  Register #(.Bits(32)) register_29 (.D(Write_Data), .C(Clock), .en(and_29_out), .Q(register_29_q));
  Register #(.Bits(32)) register_30 (.D(Write_Data), .C(Clock), .en(and_30_out), .Q(register_30_q));
  Register #(.Bits(32)) register_31 (.D(Write_Data), .C(Clock), .en(and_31_out), .Q(register_31_q));
  Register #(.Bits(32)) register_32 (.D(Write_Data), .C(Clock), .en(and_32_out), .Q(register_32_q));
  Multiplexer #(.Selector_Bits(5), .Bits(32)) multiplexer_1 (
    .sel(Read_Register_Number_1), .in_0(register_1_q), .in_1(register_2_q), .in_2(register_3_q),
    .in_3(register_4_q), .in_4(register_5_q), .in_5(register_6_q), .in_6(register_7_q), .in_7(register_8_q),
    .in_8(register_9_q), .in_9(register_10_q), .in_10(register_11_q), .in_11(register_12_q),
    .in_12(register_13_q), .in_13(register_14_q), .in_14(register_15_q), .in_15(register_16_q),
    .in_16(register_17_q), .in_17(register_18_q), .in_18(register_19_q), .in_19(register_20_q),
    .in_20(register_21_q), .in_21(register_22_q), .in_22(register_23_q), .in_23(register_24_q),
    .in_24(register_25_q), .in_25(register_26_q), .in_26(register_27_q), .in_27(register_28_q),
    .in_28(register_29_q), .in_29(register_30_q), .in_30(register_31_q), .in_31(register_32_q),
    .out(Read_Data_1));
  Multiplexer #(.Selector_Bits(5), .Bits(32)) multiplexer_2 (
    .sel(Read_Register_Number_2), .in_0(register_1_q), .in_1(register_2_q), .in_2(register_3_q),
    .in_3(register_4_q), .in_4(register_5_q), .in_5(register_6_q), .in_6(register_7_q), .in_7(register_8_q),
    .in_8(register_9_q), .in_9(register_10_q), .in_10(register_11_q), .in_11(register_12_q),
    .in_12(register_13_q), .in_13(register_14_q), .in_14(register_15_q), .in_15(register_16_q),
    .in_16(register_17_q), .in_17(register_18_q), .in_18(register_19_q), .in_19(register_20_q),
    .in_20(register_21_q), .in_21(register_22_q), .in_22(register_23_q), .in_23(register_24_q),
    .in_24(register_25_q), .in_25(register_26_q), .in_26(register_27_q), .in_27(register_28_q),
    .in_28(register_29_q), .in_29(register_30_q), .in_30(register_31_q), .in_31(register_32_q),
    .out(Read_Data_2));
endmodule
