// Digital circuit 32-Bit ALU.dig as structural Verilog
module _32_Bit_ALU (
  input  [31:0] A,
  input  [31:0] B,
  input  [3:0] Operation,
  output [31:0] Result,
  output Zero
);

  wire _1_bit_alu_1_cout, _1_bit_alu_2_cout, _1_bit_alu_3_cout, _1_bit_alu_4_cout, _1_bit_alu_5_cout,
       _1_bit_alu_6_cout, _1_bit_alu_7_cout, _1_bit_alu_8_cout, _1_bit_alu_9_cout, _1_bit_alu_10_cout,
       _1_bit_alu_11_cout, _1_bit_alu_12_cout, _1_bit_alu_13_cout, _1_bit_alu_14_cout, _1_bit_alu_15_cout,
       _1_bit_alu_16_cout, _1_bit_alu_17_cout, _1_bit_alu_18_cout, _1_bit_alu_19_cout, _1_bit_alu_20_cout,
       _1_bit_alu_21_cout, _1_bit_alu_22_cout, _1_bit_alu_23_cout, _1_bit_alu_24_cout, _1_bit_alu_25_cout,
       _1_bit_alu_26_cout, _1_bit_alu_27_cout, _1_bit_alu_28_cout, _1_bit_alu_29_cout, _1_bit_alu_30_cout,
       _1_bit_alu_31_cout, _1_bit_alu_32_set, or_1_out, or_2_out, or_3_out, or_4_out, or_5_out, or_6_out,
       or_7_out, or_8_out, or_9_out, or_10_out, or_11_out, or_12_out, or_13_out, or_14_out, or_15_out,
       or_16_out, or_17_out, or_18_out, or_19_out, or_20_out, or_21_out, or_22_out, or_23_out, or_24_out,
       or_25_out, or_26_out, or_27_out, or_28_out, or_29_out, or_30_out, or_31_out;

  _1_Bit_ALU _1_bit_alu_1 (
    .A(A[0]), .B(B[0]), .A_Invert(Operation[3]), .B_Invert(Operation[2]), .Cin(Operation[2]),
    .Less(_1_bit_alu_32_set), .Operation(Operation[1:0]), .Cout(_1_bit_alu_1_cout), .Result(Result[0]));  // open: Set
  _1_Bit_ALU _1_bit_alu_2 (
    .A(A[1]), .B(B[1]), .A_Invert(Operation[3]), .B_Invert(Operation[2]), .Cin(_1_bit_alu_1_cout),
    .Less(1'b0), .Operation(Operation[1:0]), .Cout(_1_bit_alu_2_cout), .Result(Result[1]));  // open: Set
  _1_Bit_ALU _1_bit_alu_3 (
    .A(A[2]), .B(B[2]), .A_Invert(Operation[3]), .B_Invert(Operation[2]), .Cin(_1_bit_alu_2_cout),
    .Less(1'b0), .Operation(Operation[1:0]), .Cout(_1_bit_alu_3_cout), .Result(Result[2]));  // open: Set
  _1_Bit_ALU _1_bit_alu_4 (
    .A(A[3]), .B(B[3]), .A_Invert(Operation[3]), .B_Invert(Operation[2]), .Cin(_1_bit_alu_3_cout),
    .Less(1'b0), .Operation(Operation[1:0]), .Cout(_1_bit_alu_4_cout), .Result(Result[3]));  // open: Set
  _1_Bit_ALU _1_bit_alu_5 (
    .A(A[4]), .B(B[4]), .A_Invert(Operation[3]), .B_Invert(Operation[2]), .Cin(_1_bit_alu_4_cout),
    .Less(1'b0), .Operation(Operation[1:0]), .Cout(_1_bit_alu_5_cout), .Result(Result[4]));  // open: Set
  _1_Bit_ALU _1_bit_alu_6 (
    .A(A[5]), .B(B[5]), .A_Invert(Operation[3]), .B_Invert(Operation[2]), .Cin(_1_bit_alu_5_cout),
    .Less(1'b0), .Operation(Operation[1:0]), .Cout(_1_bit_alu_6_cout), .Result(Result[5]));  // open: Set
  _1_Bit_ALU _1_bit_alu_7 (
    .A(A[6]), .B(B[6]), .A_Invert(Operation[3]), .B_Invert(Operation[2]), .Cin(_1_bit_alu_6_cout),
    .Less(1'b0), .Operation(Operation[1:0]), .Cout(_1_bit_alu_7_cout), .Result(Result[6]));  // open: Set
  _1_Bit_ALU _1_bit_alu_8 (
    .A(A[7]), .B(B[7]), .A_Invert(Operation[3]), .B_Invert(Operation[2]), .Cin(_1_bit_alu_7_cout),
    .Less(1'b0), .Operation(Operation[1:0]), .Cout(_1_bit_alu_8_cout), .Result(Result[7]));  // open: Set
  _1_Bit_ALU _1_bit_alu_9 (
    .A(A[8]), .B(B[8]), .A_Invert(Operation[3]), .B_Invert(Operation[2]), .Cin(_1_bit_alu_8_cout),
    .Less(1'b0), .Operation(Operation[1:0]), .Cout(_1_bit_alu_9_cout), .Result(Result[8]));  // open: Set
  _1_Bit_ALU _1_bit_alu_10 (
    .A(A[9]), .B(B[9]), .A_Invert(Operation[3]), .B_Invert(Operation[2]), .Cin(_1_bit_alu_9_cout),
    .Less(1'b0), .Operation(Operation[1:0]), .Cout(_1_bit_alu_10_cout), .Result(Result[9]));  // open: Set
  _1_Bit_ALU _1_bit_alu_11 (
    .A(A[10]), .B(B[10]), .A_Invert(Operation[3]), .B_Invert(Operation[2]), .Cin(_1_bit_alu_10_cout),
    .Less(1'b0), .Operation(Operation[1:0]), .Cout(_1_bit_alu_11_cout), .Result(Result[10]));  // open: Set
  _1_Bit_ALU _1_bit_alu_12 (
    .A(A[11]), .B(B[11]), .A_Invert(Operation[3]), .B_Invert(Operation[2]), .Cin(_1_bit_alu_11_cout),
    .Less(1'b0), .Operation(Operation[1:0]), .Cout(_1_bit_alu_12_cout), .Result(Result[11]));  // open: Set
  _1_Bit_ALU _1_bit_alu_13 (
    .A(A[12]), .B(B[12]), .A_Invert(Operation[3]), .B_Invert(Operation[2]), .Cin(_1_bit_alu_12_cout),
    .Less(1'b0), .Operation(Operation[1:0]), .Cout(_1_bit_alu_13_cout), .Result(Result[12]));  // open: Set
  _1_Bit_ALU _1_bit_alu_14 (
    .A(A[13]), .B(B[13]), .A_Invert(Operation[3]), .B_Invert(Operation[2]), .Cin(_1_bit_alu_13_cout),
    .Less(1'b0), .Operation(Operation[1:0]), .Cout(_1_bit_alu_14_cout), .Result(Result[13]));  // open: Set
  _1_Bit_ALU _1_bit_alu_15 (
    .A(A[14]), .B(B[14]), .A_Invert(Operation[3]), .B_Invert(Operation[2]), .Cin(_1_bit_alu_14_cout),
    .Less(1'b0), .Operation(Operation[1:0]), .Cout(_1_bit_alu_15_cout), .Result(Result[14]));  // open: Set
  _1_Bit_ALU _1_bit_alu_16 (
    .A(A[15]), .B(B[15]), .A_Invert(Operation[3]), .B_Invert(Operation[2]), .Cin(_1_bit_alu_15_cout),
    .Less(1'b0), .Operation(Operation[1:0]), .Cout(_1_bit_alu_16_cout), .Result(Result[15]));  // open: Set
  _1_Bit_ALU _1_bit_alu_17 (
    .A(A[16]), .B(B[16]), .A_Invert(Operation[3]), .B_Invert(Operation[2]), .Cin(_1_bit_alu_16_cout),
    .Less(1'b0), .Operation(Operation[1:0]), .Cout(_1_bit_alu_17_cout), .Result(Result[16]));  // open: Set
  _1_Bit_ALU _1_bit_alu_18 (
    .A(A[17]), .B(B[17]), .A_Invert(Operation[3]), .B_Invert(Operation[2]), .Cin(_1_bit_alu_17_cout),
    .Less(1'b0), .Operation(Operation[1:0]), .Cout(_1_bit_alu_18_cout), .Result(Result[17]));  // open: Set
  _1_Bit_ALU _1_bit_alu_19 (
    .A(A[18]), .B(B[18]), .A_Invert(Operation[3]), .B_Invert(Operation[2]), .Cin(_1_bit_alu_18_cout),
    .Less(1'b0), .Operation(Operation[1:0]), .Cout(_1_bit_alu_19_cout), .Result(Result[18]));  // open: Set
  _1_Bit_ALU _1_bit_alu_20 (
    .A(A[19]), .B(B[19]), .A_Invert(Operation[3]), .B_Invert(Operation[2]), .Cin(_1_bit_alu_19_cout),
    .Less(1'b0), .Operation(Operation[1:0]), .Cout(_1_bit_alu_20_cout), .Result(Result[19]));  // open: Set
  _1_Bit_ALU _1_bit_alu_21 (
    .A(A[20]), .B(B[20]), .A_Invert(Operation[3]), .B_Invert(Operation[2]), .Cin(_1_bit_alu_20_cout),
    .Less(1'b0), .Operation(Operation[1:0]), .Cout(_1_bit_alu_21_cout), .Result(Result[20]));  // open: Set
  _1_Bit_ALU _1_bit_alu_22 (
    .A(A[21]), .B(B[21]), .A_Invert(Operation[3]), .B_Invert(Operation[2]), .Cin(_1_bit_alu_21_cout),
    .Less(1'b0), .Operation(Operation[1:0]), .Cout(_1_bit_alu_22_cout), .Result(Result[21]));  // open: Set
  _1_Bit_ALU _1_bit_alu_23 (
    .A(A[22]), .B(B[22]), .A_Invert(Operation[3]), .B_Invert(Operation[2]), .Cin(_1_bit_alu_22_cout),
    .Less(1'b0), .Operation(Operation[1:0]), .Cout(_1_bit_alu_23_cout), .Result(Result[22]));  // open: Set
  _1_Bit_ALU _1_bit_alu_24 (
    .A(A[23]), .B(B[23]), .A_Invert(Operation[3]), .B_Invert(Operation[2]), .Cin(_1_bit_alu_23_cout),
    .Less(1'b0), .Operation(Operation[1:0]), .Cout(_1_bit_alu_24_cout), .Result(Result[23]));  // open: Set
  _1_Bit_ALU _1_bit_alu_25 (
    .A(A[24]), .B(B[24]), .A_Invert(Operation[3]), .B_Invert(Operation[2]), .Cin(_1_bit_alu_24_cout),
    .Less(1'b0), .Operation(Operation[1:0]), .Cout(_1_bit_alu_25_cout), .Result(Result[24]));  // open: Set
  _1_Bit_ALU _1_bit_alu_26 (
    .A(A[25]), .B(B[25]), .A_Invert(Operation[3]), .B_Invert(Operation[2]), .Cin(_1_bit_alu_25_cout),
    .Less(1'b0), .Operation(Operation[1:0]), .Cout(_1_bit_alu_26_cout), .Result(Result[25]));  // open: Set
  _1_Bit_ALU _1_bit_alu_27 (
    .A(A[26]), .B(B[26]), .A_Invert(Operation[3]), .B_Invert(Operation[2]), .Cin(_1_bit_alu_26_cout),
    .Less(1'b0), .Operation(Operation[1:0]), .Cout(_1_bit_alu_27_cout), .Result(Result[26]));  // open: Set
  _1_Bit_ALU _1_bit_alu_28 (
    .A(A[27]), .B(B[27]), .A_Invert(Operation[3]), .B_Invert(Operation[2]), .Cin(_1_bit_alu_27_cout),
    .Less(1'b0), .Operation(Operation[1:0]), .Cout(_1_bit_alu_28_cout), .Result(Result[27]));  // open: Set
  _1_Bit_ALU _1_bit_alu_29 (
    .A(A[28]), .B(B[28]), .A_Invert(Operation[3]), .B_Invert(Operation[2]), .Cin(_1_bit_alu_28_cout),
    .Less(1'b0), .Operation(Operation[1:0]), .Cout(_1_bit_alu_29_cout), .Result(Result[28]));  // open: Set
  _1_Bit_ALU _1_bit_alu_30 (
    .A(A[29]), .B(B[29]), .A_Invert(Operation[3]), .B_Invert(Operation[2]), .Cin(_1_bit_alu_29_cout),
    .Less(1'b0), .Operation(Operation[1:0]), .Cout(_1_bit_alu_30_cout), .Result(Result[29]));  // open: Set
  _1_Bit_ALU _1_bit_alu_31 (
    .A(A[30]), .B(B[30]), .A_Invert(Operation[3]), .B_Invert(Operation[2]), .Cin(_1_bit_alu_30_cout),
    .Less(1'b0), .Operation(Operation[1:0]), .Cout(_1_bit_alu_31_cout), .Result(Result[30]));  // open: Set
  _1_Bit_ALU _1_bit_alu_32 (
    .A(A[31]), .B(B[31]), .A_Invert(Operation[3]), .B_Invert(Operation[2]), .Cin(_1_bit_alu_31_cout),
    .Less(1'b0), .Operation(Operation[1:0]), .Set(_1_bit_alu_32_set), .Result(Result[31]));  // open: Cout
  or or_1 (or_1_out, Result[1], or_17_out);
  or or_2 (or_2_out, Result[3], or_18_out);
  or or_3 (or_3_out, Result[5], or_19_out);
  or or_4 (or_4_out, Result[7], or_20_out);
  or or_5 (or_5_out, Result[9], or_21_out);
  or or_6 (or_6_out, Result[11], or_22_out);
  or or_7 (or_7_out, Result[13], or_23_out);
  or or_8 (or_8_out, Result[15], or_24_out);
  or or_9 (or_9_out, Result[17], or_25_out);
  or or_10 (or_10_out, Result[19], or_26_out);
  or or_11 (or_11_out, Result[21], or_27_out);
  or or_12 (or_12_out, Result[23], or_28_out);
  or or_13 (or_13_out, Result[25], or_29_out);
  or or_14 (or_14_out, Result[27], or_30_out);
  or or_15 (or_15_out, Result[29], or_31_out);
  not not_1 (Zero, or_16_out);
  or or_16 (or_16_out, or_1_out, Result[0]);
  or or_17 (or_17_out, or_2_out, Result[2]);
  or or_18 (or_18_out, or_3_out, Result[4]);
  or or_19 (or_19_out, or_4_out, Result[6]);
  or or_20 (or_20_out, or_5_out, Result[8]);
  or or_21 (or_21_out, or_6_out, Result[10]);
  or or_22 (or_22_out, or_7_out, Result[12]);
  or or_23 (or_23_out, or_8_out, Result[14]);
  or or_24 (or_24_out, or_9_out, Result[16]);
  or or_25 (or_25_out, or_10_out, Result[18]);
  or or_26 (or_26_out, or_11_out, Result[20]);
  or or_27 (or_27_out, or_12_out, Result[22]);
  or or_28 (or_28_out, or_13_out, Result[24]);
  or or_29 (or_29_out, or_14_out, Result[26]);
  or or_30 (or_30_out, or_15_out, Result[28]);
  or or_31 (or_31_out, Result[31], Result[30]);
endmodule
