// Digital circuit 32-Bit-Register.dig as structural Verilog
module _32_Bit_Register (
  input  CLK,
  input  [31:0] D,
  output [31:0] Q
);

  _1_Bit_Register _1_bit_register_1 (.D(D[0]), .CLK(CLK), .Q(Q[0]));  // open: Q_2
  _1_Bit_Register _1_bit_register_2 (.D(D[1]), .CLK(CLK), .Q(Q[1]));  // open: Q_2
  _1_Bit_Register _1_bit_register_3 (.D(D[2]), .CLK(CLK), .Q(Q[2]));  // open: Q_2
  _1_Bit_Register _1_bit_register_4 (.D(D[3]), .CLK(CLK), .Q(Q[3]));  // open: Q_2
  _1_Bit_Register _1_bit_register_5 (.D(D[4]), .CLK(CLK), .Q(Q[4]));  // open: Q_2
  _1_Bit_Register _1_bit_register_6 (.D(D[5]), .CLK(CLK), .Q(Q[5]));  // open: Q_2
  _1_Bit_Register _1_bit_register_7 (.D(D[6]), .CLK(CLK), .Q(Q[6]));  // open: Q_2
  _1_Bit_Register _1_bit_register_8 (.D(D[7]), .CLK(CLK), .Q(Q[7]));  // open: Q_2
  _1_Bit_Register _1_bit_register_9 (.D(D[8]), .CLK(CLK), .Q(Q[8]));  // open: Q_2
  _1_Bit_Register _1_bit_register_10 (.D(D[9]), .CLK(CLK), .Q(Q[9]));  // open: Q_2
  _1_Bit_Register _1_bit_register_11 (.D(D[10]), .CLK(CLK), .Q(Q[10]));  // open: Q_2
  _1_Bit_Register _1_bit_register_12 (.D(D[11]), .CLK(CLK), .Q(Q[11]));  // open: Q_2
  _1_Bit_Register _1_bit_register_13 (.D(D[12]), .CLK(CLK), .Q(Q[12]));  // open: Q_2
  _1_Bit_Register _1_bit_register_14 (.D(D[13]), .CLK(CLK), .Q(Q[13]));  // open: Q_2
  _1_Bit_Register _1_bit_register_15 (.D(D[14]), .CLK(CLK), .Q(Q[14]));  // open: Q_2
  _1_Bit_Register _1_bit_register_16 (.D(D[15]), .CLK(CLK), .Q(Q[15]));  // open: Q_2
  _1_Bit_Register _1_bit_register_17 (.D(D[16]), .CLK(CLK), .Q(Q[16]));  // open: Q_2
  _1_Bit_Register _1_bit_register_18 (.D(D[17]), .CLK(CLK), .Q(Q[17]));  // open: Q_2
  _1_Bit_Register _1_bit_register_19 (.D(D[18]), .CLK(CLK), .Q(Q[18]));  // open: Q_2
  _1_Bit_Register _1_bit_register_20 (.D(D[19]), .CLK(CLK), .Q(Q[19]));  // open: Q_2
  _1_Bit_Register _1_bit_register_21 (.D(D[20]), .CLK(CLK), .Q(Q[20]));  // open: Q_2
  _1_Bit_Register _1_bit_register_22 (.D(D[21]), .CLK(CLK), .Q(Q[21]));  // open: Q_2
  _1_Bit_Register _1_bit_register_23 (.D(D[22]), .CLK(CLK), .Q(Q[22]));  // open: Q_2
  _1_Bit_Register _1_bit_register_24 (.D(D[23]), .CLK(CLK), .Q(Q[23]));  // open: Q_2
  _1_Bit_Register _1_bit_register_25 (.D(D[24]), .CLK(CLK), .Q(Q[24]));  // open: Q_2
  _1_Bit_Register _1_bit_register_26 (.D(D[25]), .CLK(CLK), .Q(Q[25]));  // open: Q_2
  _1_Bit_Register _1_bit_register_27 (.D(D[26]), .CLK(CLK), .Q(Q[26]));  // open: Q_2
  _1_Bit_Register _1_bit_register_28 (.D(D[27]), .CLK(CLK), .Q(Q[27]));  // open: Q_2
  _1_Bit_Register _1_bit_register_29 (.D(D[28]), .CLK(CLK), .Q(Q[28]));  // open: Q_2
  _1_Bit_Register _1_bit_register_30 (.D(D[29]), .CLK(CLK), .Q(Q[29]));  // open: Q_2
  _1_Bit_Register _1_bit_register_31 (.D(D[30]), .CLK(CLK), .Q(Q[30]));  // open: Q_2
  _1_Bit_Register _1_bit_register_32 (.D(D[31]), .CLK(CLK), .Q(Q[31]));  // open: Q_2
endmodule
