// Digital circuit 5-Bit Comparator.dig as structural Verilog
// Returns 1 if the two numbers given match, AND if they are non-zero.
// If both values are zero or if the numbers do not match, returns 0.
module _5_Bit_Comparator (
  input  [4:0] In_1,
  input  [4:0] In_2,
  output Equal
);

  wire not_1_out, or_1_out, or_2_out, xor_1_out, xor_2_out, xor_3_out, xor_4_out, xor_5_out;

  or or_1 (or_1_out, In_1[4], In_1[3], In_1[2], In_1[1], In_1[0]);
  xor xor_1 (xor_1_out, In_1[0], In_2[0]);
  xor xor_2 (xor_2_out, In_1[1], In_2[1]);
  xor xor_3 (xor_3_out, In_1[2], In_2[2]);
  xor xor_4 (xor_4_out, In_1[3], In_2[3]);
  xor xor_5 (xor_5_out, In_1[4], In_2[4]);
  or or_2 (or_2_out, xor_1_out, xor_2_out, xor_3_out, xor_4_out, xor_5_out);
  and and_1 (Equal, or_1_out, not_1_out);
  not not_1 (not_1_out, or_2_out);
endmodule
