// Digital circuit 5-bit-Register.dig as structural Verilog
module _5_bit_Register (
  input  Clock,
  input  [4:0] D,
  output [4:0] Q
);

  _1_Bit_Register _1_bit_register_1 (.D(D[0]), .CLK(Clock), .Q(Q[0]));  // open: Q_2
  _1_Bit_Register _1_bit_register_2 (.D(D[1]), .CLK(Clock), .Q(Q[1]));  // open: Q_2
  _1_Bit_Register _1_bit_register_3 (.D(D[2]), .CLK(Clock), .Q(Q[2]));  // open: Q_2
  _1_Bit_Register _1_bit_register_4 (.D(D[3]), .CLK(Clock), .Q(Q[3]));  // open: Q_2
  _1_Bit_Register _1_bit_register_5 (.D(D[4]), .CLK(Clock), .Q(Q[4]));  // open: Q_2
endmodule
