// Digital circuit 8-Bit-Register.dig as structural Verilog
module _8_Bit_Register (
  input  Clock,
  input  [7:0] D,
  output [7:0] Q
);

  _1_Bit_Register _1_bit_register_1 (.D(D[0]), .CLK(Clock), .Q(Q[0]));  // open: Q_2
  _1_Bit_Register _1_bit_register_2 (.D(D[1]), .CLK(Clock), .Q(Q[1]));  // open: Q_2
  _1_Bit_Register _1_bit_register_3 (.D(D[2]), .CLK(Clock), .Q(Q[2]));  // open: Q_2
  _1_Bit_Register _1_bit_register_4 (.D(D[3]), .CLK(Clock), .Q(Q[3]));  // open: Q_2
  _1_Bit_Register _1_bit_register_5 (.D(D[4]), .CLK(Clock), .Q(Q[4]));  // open: Q_2
  _1_Bit_Register _1_bit_register_6 (.D(D[5]), .CLK(Clock), .Q(Q[5]));  // open: Q_2
  _1_Bit_Register _1_bit_register_7 (.D(D[6]), .CLK(Clock), .Q(Q[6]));  // open: Q_2
  _1_Bit_Register _1_bit_register_8 (.D(D[7]), .CLK(Clock), .Q(Q[7]));  // open: Q_2
endmodule
