// Digital circuit ALUControl.dig as structural Verilog
module ALUControl (
  input  [1:0] ALU_Op,
  input  [3:0] Instruction_30_14_12,
  output [3:0] ALU_Control
);

  wire and_1_out, and_2_out, and_3_out, and_4_out, and_5_out, and_7_out;

  and and_1 (and_1_out, Instruction_30_14_12[2], Instruction_30_14_12[1]);
  and and_2 (and_2_out, ~ALU_Op[0], ALU_Op[1]);  // And
  and and_3 (and_3_out, ALU_Op[0], ~ALU_Op[1]);  // And
  and and_4 (and_4_out, and_1_out, ~Instruction_30_14_12[0]);  // And
  and and_5 (and_5_out, and_2_out, Instruction_30_14_12[3]);
  and and_6 (ALU_Control[0], and_2_out, and_4_out);
  and and_7 (and_7_out, and_2_out, and_1_out);
  or or_1 (ALU_Control[2], and_5_out, and_3_out);
  not not_1 (ALU_Control[1], and_7_out);

  assign ALU_Control[3] = 1'b0;
endmodule

/* Test case:
ALU_Op	Instruction[30,14:12]	ALU_Control
0b00	X	0b0010
0b01	X	0b0110
0b10	0b0000	0b0010
0b10	0b1000	0b0110
0b10	0b0111	0b0000
0b10	0b0110	0b0001
0b11	X	X
*/
