// Digital circuit Control.dig as structural Verilog
module Control (
  input  [31:0] Next_Instruction,
  input  Clock,
  input  DoBranch,
  input  [31:0] Branch_Offset,
  input  [31:0] PC,
  output [4:0] Rd,
  output RegWriteEnable,
  output [31:0] PCNext,
  output [1:0] ImmType,
  output MemToReg,
  output [3:0] ALU_Op,
  output MemWrite,
  output ForwardALURs1,
  output ForwardALURs2,
  output ALUSrc,
  output ForwardMemRs1,
  output ForwardMemRs2,
  output Stall_Generated,
  output Discard,
  output ForwardWBRs1,
  output ForwardWBRs2
);

  wire _1_bit_register_1_q, _1_bit_register_2_q, _5_bit_comparator_3_equal, _5_bit_comparator_4_equal,
       _5_bit_comparator_7_equal, _5_bit_comparator_8_equal, and_6_out, and_7_out, format_detector_1_loadop,
       not_1_out, or_3_out, Stall_Generated_q;
  wire [1:0] Flag_Gate_q_2, flag_parser_1_aluop, format_detector_1_format;
  wire [3:0] ALU_Op_Gate_q;
  wire [4:0] _5_bit_register_1_q, _5_bit_register_2_q, _5_bit_register_3_q, _5_bit_register_4_q,
       demultiplexer_1_out_0, demultiplexer_1_out_1, multiplexer_1_out, multiplexer_3_out, multiplexer_6_out,
       Rd_Gate_2_q, Rd_Gate_q;
  wire [4:4] ALU_Op_Gate_q_2;
  wire [5:0] _5_bit_comparator_1_equal;
  wire [6:0] Flag_Gate_3_q, multiplexer_4_out;
  wire [7:0] Flag_Gate_2_q, Flag_Gate_q, flag_parser_1_branch, multiplexer_5_out;
  wire [7:5] Flag_Gate_q_3;
  wire [7:6] Forwarding_Gate_q;
  wire [7:7] and_3_out;
  wire [31:0] _32_bit_register_1_q, _32_bit_register_2_q, _32_bit_register_3_q, adder_1_sum, adder_2_sum,
       adder_3_sum, Branch_Gate_2_q, Branch_Gate_3_q, Branch_Gate_q, multiplexer_7_out, shiftleft1_1_output;

  Format_Detector format_detector_1 (
    .Instruction(Next_Instruction), .Format(format_detector_1_format), .LoadOp(format_detector_1_loadop));
  Multiplexer #(.Bits(5)) multiplexer_1 (
    .sel(Discard), .in_0(Next_Instruction[11:7]), .in_1({5{1'b0}}), .out(multiplexer_1_out));
  Multiplexer #(.Bits(2)) multiplexer_2 (
    .sel(Stall_Generated), .in_0(format_detector_1_format), .in_1(2'b00), .out(ImmType));
  not not_1 (not_1_out, format_detector_1_format[0]);
  Multiplexer #(.Bits(5)) multiplexer_3 (
    .sel(not_1_out), .in_0(multiplexer_1_out), .in_1({5{1'b0}}), .out(multiplexer_3_out));
  Demultiplexer #(.Bits(5)) demultiplexer_1 (
    .sel(format_detector_1_loadop), .in(multiplexer_3_out), .out_0(demultiplexer_1_out_0),
    .out_1(demultiplexer_1_out_1));
  Multiplexer #(.Bits(7)) multiplexer_4 (
    .sel(Stall_Generated), .in_0(Next_Instruction[6:0]), .in_1(7'b0110011), .out(multiplexer_4_out));
  Multiplexer #(.Bits(8)) multiplexer_5 (
    .sel(Stall_Generated), .in_0({2'b00, _5_bit_comparator_1_equal}), .in_1({8{1'b0}}),
    .out(multiplexer_5_out));
  Multiplexer #(.Bits(5)) multiplexer_6 (
    .sel(Stall_Generated), .in_0({1'b0, Next_Instruction[30], Next_Instruction[14:12]}), .in_1({5{1'b0}}),
    .out(multiplexer_6_out));
  Adder adder_1 (.A(PC), .B(32'hfffffffc), .Sum(adder_1_sum));
  Flag_Parser flag_parser_1 (
    .OpCode(multiplexer_4_out), .Discard(Discard), .Branch(flag_parser_1_branch[0]),
    .MemRead(flag_parser_1_branch[1]), .MemtoReg(flag_parser_1_branch[2]), .ALUOp(flag_parser_1_aluop),
    .MemWrite(flag_parser_1_branch[5]), .ALUSrc(flag_parser_1_branch[6]), .RegWrite(flag_parser_1_branch[7]));
  _5_bit_Register _5_bit_register_1 (.Clock(Clock), .D(demultiplexer_1_out_1), .Q(_5_bit_register_1_q));
  _5_bit_Register _5_bit_register_2 (.Clock(Clock), .D(_5_bit_register_1_q), .Q(_5_bit_register_2_q));
  _5_Bit_Comparator _5_bit_comparator_1 (
    .In_1(Next_Instruction[19:15]), .In_2(_5_bit_register_1_q), .Equal(_5_bit_comparator_1_equal[0]));
  _5_Bit_Comparator _5_bit_comparator_2 (
    .In_1(Next_Instruction[24:20]), .In_2(_5_bit_register_1_q), .Equal(_5_bit_comparator_1_equal[1]));
  _5_bit_Register _5_bit_register_3 (.Clock(Clock), .D(demultiplexer_1_out_0), .Q(_5_bit_register_3_q));
  _32_Bit_Register Branch_Gate (.CLK(Clock), .D(adder_1_sum), .Q(Branch_Gate_q));
  _32_Bit_Register _32_bit_register_1 (.CLK(Clock), .D(Branch_Offset), .Q(_32_bit_register_1_q));
  _8_Bit_Register Flag_Gate (
    .Clock(Clock), .D({flag_parser_1_branch[7:5], flag_parser_1_aluop, flag_parser_1_branch[2:0]}),
    .Q({Flag_Gate_q_3[7], ALUSrc, Flag_Gate_q_3[5], Flag_Gate_q_2, Flag_Gate_q[2:0]}));
  _5_bit_Register Rd_Gate (.Clock(Clock), .D(Next_Instruction[11:7]), .Q(Rd_Gate_q));
  _8_Bit_Register Forwarding_Gate (
    .Clock(Clock), .D(multiplexer_5_out),
    .Q({Forwarding_Gate_q, ForwardWBRs2, ForwardWBRs1, ForwardALURs2, ForwardALURs1, ForwardMemRs2, ForwardMemRs1}));
  _5_bit_Register ALU_Op_Gate (.Clock(Clock), .D(multiplexer_6_out), .Q({ALU_Op_Gate_q_2[4], ALU_Op_Gate_q}));
  _5_Bit_Comparator _5_bit_comparator_3 (
    .In_1(Next_Instruction[19:15]), .In_2(_5_bit_register_2_q), .Equal(_5_bit_comparator_3_equal));
  _5_Bit_Comparator _5_bit_comparator_4 (
    .In_1(Next_Instruction[24:20]), .In_2(_5_bit_register_2_q), .Equal(_5_bit_comparator_4_equal));
  _5_Bit_Comparator _5_bit_comparator_5 (
    .In_1(_5_bit_register_3_q), .In_2(Next_Instruction[19:15]), .Equal(_5_bit_comparator_1_equal[2]));
  _5_Bit_Comparator _5_bit_comparator_6 (
    .In_1(_5_bit_register_3_q), .In_2(Next_Instruction[24:20]), .Equal(_5_bit_comparator_1_equal[3]));
  _5_bit_Register _5_bit_register_4 (.Clock(Clock), .D(_5_bit_register_3_q), .Q(_5_bit_register_4_q));
  _5_Bit_Comparator _5_bit_comparator_7 (
    .In_1(Next_Instruction[19:15]), .In_2(_5_bit_register_4_q), .Equal(_5_bit_comparator_7_equal));
  _5_Bit_Comparator _5_bit_comparator_8 (
    .In_1(Next_Instruction[24:20]), .In_2(_5_bit_register_4_q), .Equal(_5_bit_comparator_8_equal));
  and and_1 (Flag_Gate_q[5], Flag_Gate_q_3[5], ~Discard);  // And
  and and_2 (Flag_Gate_q[7], Flag_Gate_q_3[7], ~Discard);  // And
  ALUControl alucontrol_1 (.ALU_Op(Flag_Gate_q_2), .Instruction_30_14_12(ALU_Op_Gate_q), .ALU_Control(ALU_Op));
  or or_1 (_5_bit_comparator_1_equal[4], _5_bit_comparator_3_equal, _5_bit_comparator_7_equal);
  or or_2 (_5_bit_comparator_1_equal[5], _5_bit_comparator_4_equal, _5_bit_comparator_8_equal);
  or or_3 (or_3_out, _5_bit_comparator_1_equal[0], _5_bit_comparator_1_equal[1]);
  _32_Bit_Register Branch_Gate_2 (.CLK(Clock), .D(Branch_Gate_q), .Q(Branch_Gate_2_q));
  _32_Bit_Register _32_bit_register_2 (.CLK(Clock), .D(_32_bit_register_1_q), .Q(_32_bit_register_2_q));
  _8_Bit_Register Flag_Gate_2 (
    .Clock(Clock), .D({Flag_Gate_q[7], ALUSrc, Flag_Gate_q[5], Flag_Gate_q_2, Flag_Gate_q[2:0]}),
    .Q({Flag_Gate_2_q[7:3], MemToReg, Flag_Gate_2_q[1:0]}));
  _5_bit_Register Rd_Gate_2 (.Clock(Clock), .D(Rd_Gate_q), .Q(Rd_Gate_2_q));
  _1_Bit_Register u_Stall_Generated (.D(Stall_Generated), .CLK(Clock), .Q(Stall_Generated_q));  // open: Q_2
  and and_3 (and_3_out[7], Flag_Gate_2_q[7], ~Discard);  // And
  and and_4 (MemWrite, Flag_Gate_2_q[5], ~Discard);  // And
  and and_5 (Stall_Generated, or_3_out, ~Stall_Generated_q);  // And
  _32_Bit_Register Branch_Gate_3 (.CLK(Clock), .D(Branch_Gate_2_q), .Q(Branch_Gate_3_q));
  _32_Bit_Register _32_bit_register_3 (.CLK(Clock), .D(_32_bit_register_2_q), .Q(_32_bit_register_3_q));
  _8_Bit_Register Flag_Gate_3 (
    .Clock(Clock), .D({and_3_out[7], Flag_Gate_2_q[6:3], MemToReg, Flag_Gate_2_q[1:0]}),
    .Q({RegWriteEnable, Flag_Gate_3_q}));
  _5_bit_Register Rd_Gate_3 (.Clock(Clock), .D(Rd_Gate_2_q), .Q(Rd));
  ShiftLeft1 shiftleft1_1 (.Input(_32_bit_register_3_q), .Output(shiftleft1_1_output));
  and and_6 (and_6_out, DoBranch, Flag_Gate_3_q[0]);
  Adder adder_2 (.A(PC), .B(32'h4), .Sum(adder_2_sum));
  Adder adder_3 (.A(Branch_Gate_3_q), .B(shiftleft1_1_output), .Sum(adder_3_sum));
  Multiplexer #(.Bits(32)) multiplexer_7 (
    .sel(and_6_out), .in_0(adder_2_sum), .in_1(adder_3_sum), .out(multiplexer_7_out));
  _1_Bit_Register _1_bit_register_1 (.D(Discard), .CLK(Clock), .Q(_1_bit_register_1_q));  // open: Q_2
  Multiplexer #(.Bits(32)) multiplexer_8 (.sel(Stall_Generated), .in_0(multiplexer_7_out), .in_1(PC), .out(PCNext));
  _1_Bit_Register _1_bit_register_2 (.D(_1_bit_register_1_q), .CLK(Clock), .Q(_1_bit_register_2_q));  // open: Q_2
  and and_7 (and_7_out, ~_1_bit_register_2_q, Discard);  // And
  or or_4 (Discard, and_7_out, and_6_out);

  // Notes on the sheet:
  //   Stall Generator
  //   Decode
  //   Discard
  //   Generate Stall
  //   Load Op?
  //   ALU Op?
  //   Execute
  //   Forward ALU to Rs1
  //   Forward ALU to Rs2
  //   Forward Mem to Rs1
  //   Forward Mem to Rs2
  //   Forward WB to Rs1
  //   Forward WB to Rs2
  //   Stall Conditions Met
  //   Memory
  //   Write Back
  //   Next Instruction Fetch
  //   Do Branch
  //   And Discard
  //   Discard for Branch
  //   Do Branch
endmodule
