// Digital circuit Dual-Port ROM+RAM.dig as structural Verilog
module Dual_Port_ROM_RAM (
  input  [31:0] Data_Address,
  input  [31:0] PC_Address,
  input  Clock,
  input  Data_Write_Enable,
  input  [31:0] Write_Data,
  output [31:0] Instruction,
  output [31:0] Data
);

  wire and_1_out, or_1_out, or_2_out;
  wire [31:0] BIOS_Memory_d1, BIOS_Memory_d2, RAM_d1, RAM_d2;

  or or_1 (or_1_out, Data_Address[8], Data_Address[9], Data_Address[10], Data_Address[11], Data_Address[12], Data_Address[13], Data_Address[14], Data_Address[15], Data_Address[16], Data_Address[17], Data_Address[18], Data_Address[19], Data_Address[20], Data_Address[21], Data_Address[22], Data_Address[23]);
  or or_2 (or_2_out, PC_Address[8], PC_Address[9], PC_Address[10], PC_Address[11], PC_Address[12], PC_Address[13], PC_Address[14], PC_Address[15], PC_Address[16], PC_Address[17], PC_Address[18], PC_Address[19], PC_Address[20], PC_Address[21], PC_Address[22], PC_Address[23]);
  and and_1 (and_1_out, or_1_out, Data_Write_Enable);
  ROMDualPort #(.AddrBits(8), .Bits(32)) BIOS_Memory (
    .A1(Data_Address[7:0]), .s1(1'b1), .A2(PC_Address[7:0]), .s2(1'b1), .D1(BIOS_Memory_d1),
    .D2(BIOS_Memory_d2));
  RAMDualAccess #(.AddrBits(24), .Bits(32)) RAM (
    .str(and_1_out), .C(Clock), .ld(1'b1), .A1(Data_Address[23:0]), .Din1(Write_Data), .A2(PC_Address[23:0]),
    .D1(RAM_d1), .D2(RAM_d2));
  Multiplexer #(.Bits(32)) multiplexer_1 (.sel(or_1_out), .in_0(BIOS_Memory_d1), .in_1(RAM_d1), .out(Data));
  Multiplexer #(.Bits(32)) multiplexer_2 (.sel(or_2_out), .in_0(BIOS_Memory_d2), .in_1(RAM_d2), .out(Instruction));

  // Notes on the sheet:
  //   PC ROM or RAM?
  //   Data ROM or RAM?
  //   contents of BIOS_Memory (hex, n*v repeats v):
  //   20000413,0,0,0,2500493,0,0,0,942023,0,0,0,42903,0,0,0,409909b3
  //   ,0,0,0,fe0986e3
endmodule
