// Digital circuit Flag-Parser.dig as structural Verilog
// Parses necessary flags from OpCode.
module Flag_Parser (
  input  [6:0] OpCode,
  input  Discard,
  output Branch,
  output MemRead,
  output MemtoReg,
  output [1:0] ALUOp,
  output MemWrite,
  output ALUSrc,
  output RegWrite
);

  wire and_1_out, and_2_out, and_3_out, or_1_out, xnor_1_out;

  and and_1 (and_1_out, ~OpCode[6], ~OpCode[4]);  // And
  and and_2 (and_2_out, OpCode[5], and_1_out);
  xnor xnor_1 (xnor_1_out, OpCode[5], OpCode[4]);
  and and_3 (and_3_out, ~OpCode[6], ~OpCode[5], OpCode[4]);  // And
  and and_4 (MemRead, ~OpCode[5], and_1_out);  // And
  or or_1 (or_1_out, xnor_1_out, and_3_out);
  and and_5 (MemWrite, and_2_out, ~Discard);  // And
  or or_2 (ALUSrc, and_1_out, and_3_out);
  and and_6 (RegWrite, or_1_out, ~Discard);  // And

  assign ALUOp = {OpCode[4], OpCode[6]};
  assign Branch = OpCode[6];
  assign MemtoReg = MemRead;

  // Notes on the sheet:
  //   MemOp?
  //   Store?
  //   R/LD?
  //   ADDI?
endmodule
