// Digital circuit Format Detector.dig as structural Verilog
module Format_Detector (
  input  [31:0] Instruction,
  output [1:0] Format,
  output LoadOp
);

  wire and_1_out, and_3_out, and_4_out, and_5_out, and_6_out, and_7_out, or_1_out;
  wire [1:0] multiplexer_1_out, multiplexer_2_out, multiplexer_3_out;

  and and_1 (and_1_out, Instruction[6], Instruction[5], ~Instruction[4], ~Instruction[3], ~Instruction[2]);  // And
  and and_2 (LoadOp, ~Instruction[4], ~Instruction[5], ~Instruction[6]);  // And
  Multiplexer #(.Bits(2)) multiplexer_1 (.sel(or_1_out), .in_0(2'b00), .in_1(2'b01), .out(multiplexer_1_out));
  and and_3 (and_3_out, ~Instruction[6], ~Instruction[5], Instruction[4], ~Instruction[3], ~Instruction[2]);  // And
  Multiplexer #(.Bits(2)) multiplexer_2 (.sel(and_7_out), .in_0(2'b00), .in_1(2'b10), .out(multiplexer_2_out));
  and and_4 (and_4_out, ~Instruction[6], ~Instruction[5], ~Instruction[4], ~Instruction[3], ~Instruction[2]);  // And
  Multiplexer #(.Bits(2)) multiplexer_3 (.sel(and_1_out), .in_0(2'b00), .in_1(2'b11), .out(multiplexer_3_out));
  and and_5 (and_5_out, Instruction[6], Instruction[5], ~Instruction[4], ~Instruction[3], Instruction[2]);  // And
  or or_1 (or_1_out, and_6_out, and_5_out, and_4_out, and_3_out);
  and and_6 (and_6_out, ~Instruction[6], ~Instruction[5], Instruction[4], Instruction[3], Instruction[2]);  // And
  assign Format = multiplexer_1_out | multiplexer_2_out | multiplexer_3_out;  // Or or_2, 2 bits wide
  and and_7 (and_7_out, ~Instruction[6], Instruction[5], ~Instruction[4], ~Instruction[3], ~Instruction[2]);  // And

  // Notes on the sheet:
  //   B
  //   I
  //   S
endmodule
