// Digital circuit ImmGen.dig as structural Verilog
module ImmGen (
  input  [31:0] Instruction,
  input  [1:0] ImmType,
  output [31:0] Immediate
);

  Multiplexer #(.Bits(12), .Selector_Bits(2)) multiplexer_1 (
    .sel(ImmType), .in_0({12{1'b0}}), .in_1(Instruction[31:20]),
    .in_2({Instruction[31:25], Instruction[11:7]}),
    .in_3({Instruction[31], Instruction[7], Instruction[30:25], Instruction[11:8]}),
    .out({Immediate[31], Immediate[10:0]}));

  assign Immediate[30:11] = {20{Immediate[31]}};

  // Notes on the sheet:
  //   I-Format
  //   S-Format
  //   B-Format
endmodule
