// Digital circuit Multi-Cycle Pipelined RISC-V CPU (UNPACKED).dig as structural Verilog
module Multi_Cycle_Pipelined_RISC_V_CPU__UNPACKED (
  input  Clock,
  output [31:0] Memory_Data,
  output [31:0] Active_Instruction,
  output [31:0] ALU_Result,
  output [31:0] Current_PC,
  output [31:0] Instruction_Gate,
  output [31:0] Write_Back_Data,
  output [31:0] ALU_Op1,
  output [31:0] ALU_Op2,
  output [31:0] ALU_Immediate,
  output Write_Back_Enabled,
  output [4:0] Destination_Register
);

  wire _1_bit_register_1_q, _1_bit_register_2_q, _5_bit_comparator_3_equal, _5_bit_comparator_4_equal,
       _5_bit_comparator_7_equal, _5_bit_comparator_8_equal, _32_bit_alu_1_zero, and_1_out, and_4_out,
       and_6_out, and_7_out, and_8_out, d_ff_1_q, format_detector_1_loadop, not_1_out, not_2_out, or_3_out,
       or_4_out, Stall_Generated_q;
  wire [1:0] flag_parser_1_aluop, format_detector_1_format, multiplexer_1_out;
  wire [3:0] alucontrol_1_alu_control;
  wire [4:0] _5_bit_register_1_q, _5_bit_register_2_q, _5_bit_register_3_q, _5_bit_register_4_q,
       ALU_Op_Gate_q, demultiplexer_1_out_0, demultiplexer_1_out_1, multiplexer_2_out, multiplexer_3_out,
       multiplexer_6_out, Rd_Gate_2_q, Rd_Gate_q;
  wire [5:0] _5_bit_comparator_1_equal;
  wire [6:0] Flag_Gate_3_q, multiplexer_4_out;
  wire [7:0] Flag_Gate_2_q, Flag_Gate_q, flag_parser_1_regwrite, Forwarding_Gate_q, multiplexer_5_out;
  wire [7:5] and_2_out;
  wire [7:7] and_5_out;
  wire [31:0] _32_bit_register_1_q, _32_bit_register_2_q, _32_bit_register_3_q, _32_bit_register_4_q,
       adder_1_sum, adder_2_sum, adder_3_sum, ALU_Res_Gate_q, Branch_Gate_2_q, Branch_Gate_3_q,
       Branch_Gate_q, ImmVal_Gate_q, MemData_Gate_q, Memory_instruction, multiplexer_8_out,
       multiplexer_9_out, multiplexer_10_out, multiplexer_11_out, multiplexer_12_out, multiplexer_14_out,
       multiplexer_16_out, multiplexer_17_out, Registers_read_data_1, Registers_read_data_2, RegVal_Gate_q,
       shiftleft1_1_output;

  PC PC (.PCNext(multiplexer_17_out), .Clock_In(Clock), .PC(Current_PC));
  Format_Detector format_detector_1 (
    .Instruction(Instruction_Gate), .Format(format_detector_1_format), .LoadOp(format_detector_1_loadop));
  and and_1 (and_1_out, ~and_6_out, not_1_out);  // And
  not not_1 (not_1_out, Clock);
  Multiplexer #(.Bits(2)) multiplexer_1 (
    .sel(and_6_out), .in_0(format_detector_1_format), .in_1(2'b00), .out(multiplexer_1_out));
  Multiplexer #(.Bits(5)) multiplexer_2 (
    .sel(or_4_out), .in_0(Instruction_Gate[11:7]), .in_1({5{1'b0}}), .out(multiplexer_2_out));
  _32_Bit_Register u_Instruction_Gate (.CLK(and_1_out), .D(Memory_instruction), .Q(Instruction_Gate));
  Multiplexer #(.Bits(5)) multiplexer_3 (
    .sel(not_2_out), .in_0(multiplexer_2_out), .in_1({5{1'b0}}), .out(multiplexer_3_out));
  not not_2 (not_2_out, format_detector_1_format[0]);
  Multiplexer #(.Bits(7)) multiplexer_4 (
    .sel(and_6_out), .in_0(Instruction_Gate[6:0]), .in_1(7'b0110011), .out(multiplexer_4_out));
  Multiplexer #(.Bits(8)) multiplexer_5 (
    .sel(and_6_out), .in_0({2'b00, _5_bit_comparator_1_equal}), .in_1({8{1'b0}}), .out(multiplexer_5_out));
  Multiplexer #(.Bits(5)) multiplexer_6 (
    .sel(and_6_out), .in_0({1'b0, Instruction_Gate[30], Instruction_Gate[14:12]}), .in_1({5{1'b0}}),
    .out(multiplexer_6_out));
  Multiplexer #(.Bits(32)) multiplexer_7 (
    .sel(and_6_out), .in_0(Instruction_Gate), .in_1(32'h33), .out(Active_Instruction));
  Demultiplexer #(.Bits(5)) demultiplexer_1 (
    .sel(format_detector_1_loadop), .in(multiplexer_3_out), .out_0(demultiplexer_1_out_0),
    .out_1(demultiplexer_1_out_1));
  _5_bit_Register _5_bit_register_1 (.Clock(not_1_out), .D(demultiplexer_1_out_1), .Q(_5_bit_register_1_q));
  Adder adder_1 (.A(Current_PC), .B(32'hfffffffc), .Sum(adder_1_sum));
  Flag_Parser flag_parser_1 (
    .OpCode(multiplexer_4_out), .Discard(or_4_out), .Branch(flag_parser_1_regwrite[0]),
    .MemRead(flag_parser_1_regwrite[1]), .MemtoReg(flag_parser_1_regwrite[2]), .ALUOp(flag_parser_1_aluop),
    .MemWrite(flag_parser_1_regwrite[5]), .ALUSrc(flag_parser_1_regwrite[6]),
    .RegWrite(flag_parser_1_regwrite[7]));
  _5_bit_Register _5_bit_register_2 (.Clock(not_1_out), .D(_5_bit_register_1_q), .Q(_5_bit_register_2_q));
  _32_32_bit_Register_File Registers (
    .Read_Register_Number_1(Active_Instruction[19:15]), .Read_Register_Number_2(Active_Instruction[24:20]),
    .Write_Data(Write_Back_Data), .Write_Enable(Write_Back_Enabled),
    .Write_Register_Number(Destination_Register), .Clock(Clock), .Read_Data_1(Registers_read_data_1),
    .Read_Data_2(Registers_read_data_2));
  _5_Bit_Comparator _5_bit_comparator_1 (
    .In_1(Instruction_Gate[19:15]), .In_2(_5_bit_register_1_q), .Equal(_5_bit_comparator_1_equal[0]));
  _5_Bit_Comparator _5_bit_comparator_2 (
    .In_1(Instruction_Gate[24:20]), .In_2(_5_bit_register_1_q), .Equal(_5_bit_comparator_1_equal[1]));
  _5_bit_Register _5_bit_register_3 (.Clock(not_1_out), .D(demultiplexer_1_out_0), .Q(_5_bit_register_3_q));
  _32_Bit_Register Branch_Gate (.CLK(not_1_out), .D(adder_1_sum), .Q(Branch_Gate_q));
  _32_Bit_Register _32_bit_register_1 (.CLK(not_1_out), .D(ALU_Immediate), .Q(_32_bit_register_1_q));
  _8_Bit_Register Flag_Gate (
    .Clock(not_1_out), .D({flag_parser_1_regwrite[7:5], flag_parser_1_aluop, flag_parser_1_regwrite[2:0]}),
    .Q(Flag_Gate_q));
  _5_bit_Register Rd_Gate (.Clock(not_1_out), .D(Instruction_Gate[11:7]), .Q(Rd_Gate_q));
  _8_Bit_Register Forwarding_Gate (.Clock(not_1_out), .D(multiplexer_5_out), .Q(Forwarding_Gate_q));
  _5_bit_Register ALU_Op_Gate (.Clock(not_1_out), .D(multiplexer_6_out), .Q(ALU_Op_Gate_q));
  ImmGen ImmGen (.Instruction(Active_Instruction), .ImmType(multiplexer_1_out), .Immediate(ALU_Immediate));
  Dual_Port_ROM_RAM Memory (
    .Data_Address(ALU_Res_Gate_q), .PC_Address(Current_PC), .Clock(Clock), .Data_Write_Enable(and_4_out),
    .Write_Data(MemData_Gate_q), .Instruction(Memory_instruction), .Data(Memory_Data));
  _5_Bit_Comparator _5_bit_comparator_3 (
    .In_1(Instruction_Gate[19:15]), .In_2(_5_bit_register_2_q), .Equal(_5_bit_comparator_3_equal));
  _5_Bit_Comparator _5_bit_comparator_4 (
    .In_1(Instruction_Gate[24:20]), .In_2(_5_bit_register_2_q), .Equal(_5_bit_comparator_4_equal));
  _5_bit_Register _5_bit_register_4 (.Clock(not_1_out), .D(_5_bit_register_3_q), .Q(_5_bit_register_4_q));
  _5_Bit_Comparator _5_bit_comparator_5 (
    .In_1(_5_bit_register_3_q), .In_2(Instruction_Gate[19:15]), .Equal(_5_bit_comparator_1_equal[2]));
  _5_Bit_Comparator _5_bit_comparator_6 (
    .In_1(_5_bit_register_3_q), .In_2(Instruction_Gate[24:20]), .Equal(_5_bit_comparator_1_equal[3]));
  _5_Bit_Comparator _5_bit_comparator_7 (
    .In_1(Instruction_Gate[19:15]), .In_2(_5_bit_register_4_q), .Equal(_5_bit_comparator_7_equal));
  _5_Bit_Comparator _5_bit_comparator_8 (
    .In_1(Instruction_Gate[24:20]), .In_2(_5_bit_register_4_q), .Equal(_5_bit_comparator_8_equal));
  and and_2 (and_2_out[5], Flag_Gate_q[5], ~or_4_out);  // And
  and and_3 (and_2_out[7], Flag_Gate_q[7], ~or_4_out);  // And
  ALUControl alucontrol_1 (
    .ALU_Op(Flag_Gate_q[4:3]), .Instruction_30_14_12(ALU_Op_Gate_q[3:0]),
    .ALU_Control(alucontrol_1_alu_control));
  _32_Bit_Register RegVal_Gate (.CLK(not_1_out), .D(Registers_read_data_1), .Q(RegVal_Gate_q));
  _32_Bit_Register _32_bit_register_2 (.CLK(not_1_out), .D(Registers_read_data_2), .Q(_32_bit_register_2_q));
  _32_Bit_Register ImmVal_Gate (.CLK(not_1_out), .D(ALU_Immediate), .Q(ImmVal_Gate_q));
  or or_1 (_5_bit_comparator_1_equal[4], _5_bit_comparator_3_equal, _5_bit_comparator_7_equal);
  or or_2 (_5_bit_comparator_1_equal[5], _5_bit_comparator_4_equal, _5_bit_comparator_8_equal);
  Multiplexer #(.Bits(32)) multiplexer_8 (
    .sel(Flag_Gate_2_q[2]), .in_0(ALU_Res_Gate_q), .in_1(Memory_Data), .out(multiplexer_8_out));
  Multiplexer #(.Bits(32)) multiplexer_9 (
    .sel(Forwarding_Gate_q[2]), .in_0(RegVal_Gate_q), .in_1(ALU_Res_Gate_q), .out(multiplexer_9_out));
  Multiplexer #(.Bits(32)) multiplexer_10 (
    .sel(Forwarding_Gate_q[3]), .in_0(_32_bit_register_2_q), .in_1(ALU_Res_Gate_q), .out(multiplexer_10_out));
  _32_Bit_Register Branch_Gate_2 (.CLK(not_1_out), .D(Branch_Gate_q), .Q(Branch_Gate_2_q));
  _32_Bit_Register _32_bit_register_3 (.CLK(not_1_out), .D(_32_bit_register_1_q), .Q(_32_bit_register_3_q));
  _8_Bit_Register Flag_Gate_2 (
    .Clock(not_1_out), .D({and_2_out[7], Flag_Gate_q[6], and_2_out[5], Flag_Gate_q[4:0]}), .Q(Flag_Gate_2_q));
  _5_bit_Register Rd_Gate_2 (.Clock(not_1_out), .D(Rd_Gate_q), .Q(Rd_Gate_2_q));
  _32_Bit_Register WB_Gate (.CLK(not_1_out), .D(multiplexer_8_out), .Q(Write_Back_Data));
  or or_3 (or_3_out, _5_bit_comparator_1_equal[0], _5_bit_comparator_1_equal[1]);
  Multiplexer #(.Bits(32)) multiplexer_11 (
    .sel(Forwarding_Gate_q[0]), .in_0(multiplexer_9_out), .in_1(Memory_Data), .out(multiplexer_11_out));
  Multiplexer #(.Bits(32)) multiplexer_12 (
    .sel(Forwarding_Gate_q[1]), .in_0(multiplexer_10_out), .in_1(Memory_Data), .out(multiplexer_12_out));
  and and_4 (and_4_out, Flag_Gate_2_q[5], ~or_4_out);  // And
  Multiplexer #(.Bits(32)) multiplexer_13 (
    .sel(Forwarding_Gate_q[4]), .in_0(multiplexer_11_out), .in_1(Write_Back_Data), .out(ALU_Op1));
  Multiplexer #(.Bits(32)) multiplexer_14 (
    .sel(Forwarding_Gate_q[5]), .in_0(multiplexer_12_out), .in_1(Write_Back_Data), .out(multiplexer_14_out));
  _1_Bit_Register Stall_Generated (.D(and_6_out), .CLK(not_1_out), .Q(Stall_Generated_q));  // open: Q_2
  and and_5 (and_5_out[7], Flag_Gate_2_q[7], ~or_4_out);  // And
  Multiplexer #(.Bits(32)) multiplexer_15 (
    .sel(Flag_Gate_q[6]), .in_0(multiplexer_14_out), .in_1(ImmVal_Gate_q), .out(ALU_Op2));
  and and_6 (and_6_out, or_3_out, ~Stall_Generated_q);  // And
  _32_Bit_ALU _32_bit_alu_1 (
    .A(ALU_Op1), .B(ALU_Op2), .Operation(alucontrol_1_alu_control), .Result(ALU_Result),
    .Zero(_32_bit_alu_1_zero));
  _32_Bit_Register Branch_Gate_3 (.CLK(not_1_out), .D(Branch_Gate_2_q), .Q(Branch_Gate_3_q));
  _32_Bit_Register _32_bit_register_4 (.CLK(not_1_out), .D(_32_bit_register_3_q), .Q(_32_bit_register_4_q));
  _8_Bit_Register Flag_Gate_3 (
    .Clock(not_1_out), .D({and_5_out[7], Flag_Gate_2_q[6:0]}), .Q({Write_Back_Enabled, Flag_Gate_3_q}));
  _5_bit_Register Rd_Gate_3 (.Clock(not_1_out), .D(Rd_Gate_2_q), .Q(Destination_Register));
  _32_Bit_Register ALU_Res_Gate (.CLK(not_1_out), .D(ALU_Result), .Q(ALU_Res_Gate_q));
  D_FF d_ff_1 (.D(_32_bit_alu_1_zero), .C(not_1_out), .Q(d_ff_1_q));  // open: nQ
  _32_Bit_Register MemData_Gate (.CLK(not_1_out), .D(multiplexer_10_out), .Q(MemData_Gate_q));
  Adder adder_2 (.A(Current_PC), .B(32'h4), .Sum(adder_2_sum));
  Adder adder_3 (.A(Branch_Gate_3_q), .B(shiftleft1_1_output), .Sum(adder_3_sum));
  ShiftLeft1 shiftleft1_1 (.Input(_32_bit_register_4_q), .Output(shiftleft1_1_output));
  and and_7 (and_7_out, d_ff_1_q, Flag_Gate_3_q[0]);
  Multiplexer #(.Bits(32)) multiplexer_16 (
    .sel(and_7_out), .in_0(adder_2_sum), .in_1(adder_3_sum), .out(multiplexer_16_out));
  Multiplexer #(.Bits(32)) multiplexer_17 (
    .sel(and_6_out), .in_0(multiplexer_16_out), .in_1(Current_PC), .out(multiplexer_17_out));
  _1_Bit_Register _1_bit_register_1 (.D(or_4_out), .CLK(not_1_out), .Q(_1_bit_register_1_q));  // open: Q_2
  _1_Bit_Register _1_bit_register_2 (.D(_1_bit_register_1_q), .CLK(not_1_out), .Q(_1_bit_register_2_q));  // open: Q_2
  and and_8 (and_8_out, ~_1_bit_register_2_q, or_4_out);  // And
  or or_4 (or_4_out, and_8_out, and_7_out);

  // Notes on the sheet:
  //   Stall Generator
  //   Gate Update
  //   Decode
  //   Next Instruction
  //   Discard
  //   Immediate
  //   Load Op?
  //   Generate Stall
  //   ALU Op?
  //   Execute
  //   ZERO Flag
  //   Write Back Data
  //   Forward ALU to Rs1
  //   Forward ALU to Rs2
  //   ALU Result
  //   Memory Store Data
  //   ALU-1
  //   ALU-2
  //   Gate Update Clock Line
  //   Forward Mem to Rs1
  //   Forward Mem to Rs2
  //   Forward WB to Rs1
  //   Forward WB to Rs2
  //   Memory
  //   MEM-1
  //   MEM-2
  //   Memory Write Enable
  //   Stall Conditions Met
  //   WB-1
  //   WB-2
  //   S-IMM
  //   RS2/ALU-2
  //   Do Branch
  //   And Discard
  //   Write Back
  //   Next Instruction Fetch
  //   Discard for Branch
  //   Do Branch
endmodule
