// Digital circuit Multi-Cycle Pipelined RISC-V CPU.dig as structural Verilog
module Multi_Cycle_Pipelined_RISC_V_CPU (
  input  Clock,
  output [31:0] Memory_Data,
  output [31:0] Active_Instruction,
  output [31:0] ALU_Result,
  output Stall_Generated,
  output [31:0] Current_PC,
  output [31:0] Instruction_Gate,
  output Discard,
  output [31:0] Write_Back_Data,
  output [31:0] ALU_Op1,
  output [31:0] ALU_Op2,
  output [31:0] ALU_Immediate,
  output Write_Back_Enabled,
  output [4:0] Destination_Register
);

  wire _32_bit_alu_1_zero, and_1_out, Control_alusrc, Control_forwardalurs1, Control_forwardalurs2,
       Control_forwardmemrs1, Control_forwardmemrs2, Control_forwardwbrs1, Control_forwardwbrs2,
       Control_memtoreg, Control_memwrite, d_ff_1_q, not_1_out;
  wire [1:0] Control_immtype;
  wire [3:0] Control_alu_op;
  wire [31:0] _32_bit_register_1_q, ALU_Res_Gate_q, Control_pcnext, ImmVal_Gate_q, MemData_Gate_q,
       Memory_instruction, multiplexer_2_out, multiplexer_3_out, multiplexer_4_out, multiplexer_5_out,
       multiplexer_6_out, multiplexer_8_out, Registers_read_data_1, Registers_read_data_2, RegVal_Gate_q;

  PC PC (.PCNext(Control_pcnext), .Clock_In(Clock), .PC(Current_PC));
  and and_1 (and_1_out, ~Stall_Generated, not_1_out);  // And
  not not_1 (not_1_out, Clock);
  _32_Bit_Register u_Instruction_Gate (.CLK(and_1_out), .D(Memory_instruction), .Q(Instruction_Gate));
  Multiplexer #(.Bits(32)) multiplexer_1 (
    .sel(Stall_Generated), .in_0(Instruction_Gate), .in_1(32'h33), .out(Active_Instruction));
  Control Control (
    .Next_Instruction(Instruction_Gate), .Clock(not_1_out), .DoBranch(d_ff_1_q),
    .Branch_Offset(ALU_Immediate), .PC(Current_PC), .Rd(Destination_Register),
    .RegWriteEnable(Write_Back_Enabled), .PCNext(Control_pcnext), .ImmType(Control_immtype),
    .MemToReg(Control_memtoreg), .ALU_Op(Control_alu_op), .MemWrite(Control_memwrite),
    .ForwardALURs1(Control_forwardalurs1), .ForwardALURs2(Control_forwardalurs2), .ALUSrc(Control_alusrc),
    .ForwardMemRs1(Control_forwardmemrs1), .ForwardMemRs2(Control_forwardmemrs2),
    .Stall_Generated(Stall_Generated), .Discard(Discard), .ForwardWBRs1(Control_forwardwbrs1),
    .ForwardWBRs2(Control_forwardwbrs2));
  _32_32_bit_Register_File Registers (
    .Read_Register_Number_1(Active_Instruction[19:15]), .Read_Register_Number_2(Active_Instruction[24:20]),
    .Write_Data(Write_Back_Data), .Write_Enable(Write_Back_Enabled),
    .Write_Register_Number(Destination_Register), .Clock(Clock), .Read_Data_1(Registers_read_data_1),
    .Read_Data_2(Registers_read_data_2));
  ImmGen ImmGen (.Instruction(Active_Instruction), .ImmType(Control_immtype), .Immediate(ALU_Immediate));
  Dual_Port_ROM_RAM Memory (
    .Data_Address(ALU_Res_Gate_q), .PC_Address(Current_PC), .Clock(Clock),
    .Data_Write_Enable(Control_memwrite), .Write_Data(MemData_Gate_q), .Instruction(Memory_instruction),
    .Data(Memory_Data));
  _32_Bit_Register RegVal_Gate (.CLK(not_1_out), .D(Registers_read_data_1), .Q(RegVal_Gate_q));
  _32_Bit_Register _32_bit_register_1 (.CLK(not_1_out), .D(Registers_read_data_2), .Q(_32_bit_register_1_q));
  _32_Bit_Register ImmVal_Gate (.CLK(not_1_out), .D(ALU_Immediate), .Q(ImmVal_Gate_q));
  Multiplexer #(.Bits(32)) multiplexer_2 (
    .sel(Control_memtoreg), .in_0(ALU_Res_Gate_q), .in_1(Memory_Data), .out(multiplexer_2_out));
  Multiplexer #(.Bits(32)) multiplexer_3 (
    .sel(Control_forwardalurs1), .in_0(RegVal_Gate_q), .in_1(ALU_Res_Gate_q), .out(multiplexer_3_out));
  Multiplexer #(.Bits(32)) multiplexer_4 (
    .sel(Control_forwardalurs2), .in_0(_32_bit_register_1_q), .in_1(ALU_Res_Gate_q), .out(multiplexer_4_out));
  _32_Bit_Register WB_Gate (.CLK(not_1_out), .D(multiplexer_2_out), .Q(Write_Back_Data));
  Multiplexer #(.Bits(32)) multiplexer_5 (
    .sel(Control_forwardmemrs1), .in_0(multiplexer_3_out), .in_1(Memory_Data), .out(multiplexer_5_out));
  Multiplexer #(.Bits(32)) multiplexer_6 (
    .sel(Control_forwardmemrs2), .in_0(multiplexer_4_out), .in_1(Memory_Data), .out(multiplexer_6_out));
  Multiplexer #(.Bits(32)) multiplexer_7 (
    .sel(Control_forwardwbrs1), .in_0(multiplexer_5_out), .in_1(Write_Back_Data), .out(ALU_Op1));
  Multiplexer #(.Bits(32)) multiplexer_8 (
    .sel(Control_forwardwbrs2), .in_0(multiplexer_6_out), .in_1(Write_Back_Data), .out(multiplexer_8_out));
  Multiplexer #(.Bits(32)) multiplexer_9 (
    .sel(Control_alusrc), .in_0(multiplexer_8_out), .in_1(ImmVal_Gate_q), .out(ALU_Op2));
  _32_Bit_ALU _32_bit_alu_1 (
    .A(ALU_Op1), .B(ALU_Op2), .Operation(Control_alu_op), .Result(ALU_Result), .Zero(_32_bit_alu_1_zero));
  _32_Bit_Register ALU_Res_Gate (.CLK(not_1_out), .D(ALU_Result), .Q(ALU_Res_Gate_q));
  D_FF d_ff_1 (.D(_32_bit_alu_1_zero), .C(not_1_out), .Q(d_ff_1_q));  // open: nQ
  _32_Bit_Register MemData_Gate (.CLK(not_1_out), .D(multiplexer_4_out), .Q(MemData_Gate_q));

  // Notes on the sheet:
  //   Clock: Hz: 4
  //   Gate Update
  //   Next Instruction
  //   Immediate
  //   ZERO Flag
  //   Write Back Data
  //   ALU Result
  //   Memory Store Data
  //   ALU-1
  //   ALU-2
  //   Gate Update Clock Line
  //   MEM-1
  //   MEM-2
  //   Memory Write Enable
  //   WB-1
  //   WB-2
  //   S-IMM
  //   RS2/ALU-2
endmodule
