// Digital circuit PC.dig as structural Verilog
module PC (
  input  [31:0] PCNext,
  input  Clock_In,
  output [31:0] PC
);

  _32_Bit_Register _32_bit_register_1 (.CLK(Clock_In), .D(PCNext), .Q(PC));
endmodule
