// Digital circuit ShiftLeft1.dig as structural Verilog
module ShiftLeft1 (
  input  [31:0] Input,
  output [31:0] Output
);

  BarrelShifter #(.Bits(32)) barrelshifter_1 (.in(Input), .shift(6'b000001), .out(Output));
endmodule
